// Logisim project LAB5.circ as structural Verilog: 8 circuits, main circuit main
module main (
  input  in_1,
  input  in_2,
  input  [1:0] S,
  input  M
);

  wire leda_1_x, ledb_1_x, ledc_1_x, ledd_1_x, lede_1_x, ledf_1_x, multiplexer_1_out, multiplexer_2_out,
       multiplexer_3_out, multiplexer_4_out, not_1_out, or_1_out;

  not not_1 (not_1_out, M);
  or or_1 (or_1_out, S[0], S[1], M);
  Multiplexer #(.select(2)) multiplexer_1 (
    .in0(not_1_out), .in1(in_2), .in2(in_2), .in3(not_1_out), .out(multiplexer_1_out), .sel(S), .en(or_1_out));
  Multiplexer #(.select(2)) multiplexer_2 (
    .in0(not_1_out), .in1(M), .in2(in_1), .in3(in_2), .out(multiplexer_2_out), .sel(S), .en(or_1_out));
  Multiplexer #(.select(2)) multiplexer_3 (
    .in0(M), .in1(not_1_out), .in2(M), .in3(in_2), .out(multiplexer_3_out), .sel(S), .en(or_1_out));
  Multiplexer #(.select(2)) multiplexer_4 (
    .in0(not_1_out), .in1(in_1), .in2(in_1), .in3(in_2), .out(multiplexer_4_out), .sel(S), .en(or_1_out));
  LEDA leda_1 (
    .a(multiplexer_1_out), .b(multiplexer_2_out), .c(multiplexer_3_out), .d(multiplexer_4_out), .x(leda_1_x));
  LEDB ledb_1 (
    .a(multiplexer_1_out), .b(multiplexer_2_out), .c(multiplexer_3_out), .d(multiplexer_4_out), .x(ledb_1_x));
  LEDC ledc_1 (
    .a(multiplexer_1_out), .b(multiplexer_2_out), .c(multiplexer_3_out), .d(multiplexer_4_out), .x(ledc_1_x));
  LEDD ledd_1 (
    .a(multiplexer_1_out), .b(multiplexer_2_out), .c(multiplexer_3_out), .d(multiplexer_4_out), .x(ledd_1_x));
  LEDE lede_1 (
    .a(multiplexer_1_out), .b(multiplexer_2_out), .c(multiplexer_3_out), .d(multiplexer_4_out), .x(lede_1_x));
  LEDF ledf_1 (
    .a(multiplexer_1_out), .b(multiplexer_2_out), .c(multiplexer_3_out), .d(multiplexer_4_out), .x(ledf_1_x));
  LEDG ledg_1 (
    .a(multiplexer_1_out), .b(multiplexer_2_out), .c(multiplexer_3_out), .d(multiplexer_4_out), .x(ledd_1_x));
  _7_Segment_Display u_7_segment_display_1 (
    .g(ledd_1_x), .f(ledf_1_x), .a(leda_1_x), .b(ledb_1_x), .e(lede_1_x), .d(ledd_1_x), .c(ledc_1_x));  // open: dp

  // Notes on the sheet:
  //   C
endmodule

module LEDA (
  input  a,
  input  b,
  input  c,
  input  d,
  output x
);

  wire and_1_out, and_2_out, and_3_out, and_4_out, and_5_out, and_6_out, and_7_out, and_8_out, and_9_out,
       and_10_out, not_1_out, not_2_out, not_3_out, not_4_out, not_5_out, not_6_out, not_7_out, not_8_out,
       not_9_out, or_1_out, or_2_out, or_3_out;

  not not_1 (not_1_out, a);
  and and_1 (and_1_out, not_1_out, not_2_out);
  not not_2 (not_2_out, b);
  not not_3 (not_3_out, d);
  not not_4 (not_4_out, a);
  and and_2 (and_2_out, not_4_out, not_5_out);
  not not_5 (not_5_out, b);
  not not_6 (not_6_out, a);
  not not_7 (not_7_out, b);
  not not_8 (not_8_out, c);
  and and_3 (and_3_out, and_1_out, not_3_out);
  and and_4 (and_4_out, and_2_out, c);
  and and_5 (and_5_out, not_6_out, b);
  and and_6 (and_6_out, a, not_7_out);
  not not_9 (not_9_out, c);
  and and_7 (and_7_out, a, not_8_out);
  or or_1 (or_1_out, and_3_out, and_4_out);
  and and_8 (and_8_out, and_5_out, d);
  and and_9 (and_9_out, and_6_out, not_9_out);
  and and_10 (and_10_out, and_7_out, d);
  or or_2 (or_2_out, or_1_out, and_8_out);
  or or_3 (or_3_out, and_9_out, and_10_out);
  or or_4 (x, or_2_out, or_3_out);
endmodule

module LEDB (
  input  a,
  input  b,
  input  c,
  input  d,
  output x
);

  wire and_1_out, and_2_out, and_3_out, and_4_out, and_5_out, not_1_out, not_2_out, not_3_out, not_4_out,
       not_5_out, not_6_out, not_7_out, or_1_out, or_2_out;

  not not_1 (not_1_out, a);
  not not_2 (not_2_out, b);
  not not_3 (not_3_out, b);
  not not_4 (not_4_out, c);
  not not_5 (not_5_out, c);
  not not_6 (not_6_out, d);
  not not_7 (not_7_out, a);
  and and_1 (and_1_out, not_7_out, c);
  and and_2 (and_2_out, not_1_out, not_2_out);
  and and_3 (and_3_out, not_3_out, not_4_out);
  and and_4 (and_4_out, not_5_out, not_6_out);
  and and_5 (and_5_out, and_1_out, d);
  or or_1 (or_1_out, and_2_out, and_3_out);
  or or_2 (or_2_out, and_4_out, and_5_out);
  or or_3 (x, or_1_out, or_2_out);
endmodule

module LEDC (
  input  a,
  input  b,
  input  c,
  input  d,
  output x
);

  wire and_1_out, and_2_out, and_3_out, not_1_out, not_2_out, not_3_out, not_4_out, or_1_out;

  not not_1 (not_1_out, b);
  and and_1 (and_1_out, not_1_out, not_2_out);
  not not_2 (not_2_out, c);
  not not_3 (not_3_out, b);
  and and_2 (and_2_out, not_3_out, d);
  not not_4 (not_4_out, a);
  or or_1 (or_1_out, and_1_out, and_2_out);
  and and_3 (and_3_out, not_4_out, b);
  or or_2 (x, or_1_out, and_3_out);
endmodule

module LEDD (
  input  a,
  input  b,
  input  c,
  input  d,
  output x
);

  wire and_1_out, and_2_out, and_3_out, and_4_out, and_5_out, not_1_out, not_2_out, not_3_out, not_4_out,
       not_5_out, or_1_out, or_2_out;

  not not_1 (not_1_out, b);
  not not_2 (not_2_out, d);
  not not_3 (not_3_out, b);
  not not_4 (not_4_out, d);
  and and_1 (and_1_out, b, not_5_out);
  not not_5 (not_5_out, c);
  and and_2 (and_2_out, not_1_out, not_2_out);
  and and_3 (and_3_out, not_3_out, c);
  and and_4 (and_4_out, c, not_4_out);
  and and_5 (and_5_out, and_1_out, d);
  or or_1 (or_1_out, and_2_out, and_3_out);
  or or_2 (or_2_out, and_4_out, and_5_out);
  or or_3 (x, or_1_out, or_2_out);
endmodule

module LEDE (
  input  a,
  input  b,
  input  c,
  input  d,
  output x
);

  wire and_1_out, and_2_out, not_1_out, not_2_out, not_3_out;

  not not_1 (not_1_out, b);
  and and_1 (and_1_out, not_1_out, not_2_out);
  not not_2 (not_2_out, d);
  and and_2 (and_2_out, c, not_3_out);
  not not_3 (not_3_out, d);
  or or_1 (x, and_1_out, and_2_out);
endmodule

module LEDF (
  input  a,
  input  b,
  input  c,
  input  d,
  output x
);

  wire and_1_out, and_2_out, and_3_out, and_4_out, not_1_out, not_2_out, not_3_out, not_4_out, not_5_out,
       or_1_out, or_2_out;

  not not_1 (not_1_out, c);
  and and_1 (and_1_out, not_1_out, not_2_out);
  not not_2 (not_2_out, d);
  and and_2 (and_2_out, b, not_3_out);
  not not_3 (not_3_out, c);
  and and_3 (and_3_out, b, not_4_out);
  not not_4 (not_4_out, d);
  and and_4 (and_4_out, a, not_5_out);
  not not_5 (not_5_out, c);
  or or_1 (or_1_out, and_1_out, and_2_out);
  or or_2 (or_2_out, and_3_out, and_4_out);
  or or_3 (x, or_1_out, or_2_out);
endmodule

module LEDG (
  input  a,
  input  b,
  input  c,
  input  d,
  output x
);

  wire and_1_out, and_2_out, and_3_out, and_4_out, not_1_out, not_2_out, not_3_out, not_4_out, or_1_out,
       or_2_out;

  not not_1 (not_1_out, b);
  and and_1 (and_1_out, not_1_out, c);
  and and_2 (and_2_out, b, not_2_out);
  not not_2 (not_2_out, c);
  and and_3 (and_3_out, b, not_3_out);
  not not_3 (not_3_out, d);
  and and_4 (and_4_out, a, not_4_out);
  not not_4 (not_4_out, b);
  or or_1 (or_1_out, and_1_out, and_2_out);
  or or_2 (or_2_out, and_3_out, and_4_out);
  or or_3 (x, or_1_out, or_2_out);
endmodule
